# Fritzing sketch circuit (saved by Fritzing 0.9.3b)
breadboards: 1

parts:
  Part1 = Arduino Mega 2560 (Rev3)
  U1 = POT [package=pot_mammoth]
  S1 = Pushbutton [package="[THT]"]
  S2 = Pushbutton [package="[THT]"]
  LED1 = LED - 3mm [color="Red (633nm)" package="3 mm [THT]"]
  LED2 = LED - 3mm [color="Red (633nm)" package="3 mm [THT]"]
  S3 = Pushbutton [package="[THT]"]
  LED3 = LED - 3mm [color="Red (633nm)" package="3 mm [THT]"]
  S4 = Pushbutton [package="[THT]"]
  LED4 = LED - 3mm [color="Red (633nm)" package="3 mm [THT]"]
  S5 = Pushbutton [package="[THT]"]
  LED5 = LED - 3mm [color="Red (633nm)" package="3 mm [THT]"]
  Part2 = RFID-RC522-v2
  Part3 = LCD1602-I2C
  SG1 = Buzzer 12mm [part_number=COM-07950 package=buzzer-12mm-ns]

nets:
  N1: Part1.A0, U1.A
  N2: Part1.D21/SCL, Part3.SCL
  N3: Part1.D20/SDA, Part3.SDA
  GND: Part1.GND, U1.S, S1.Pin_1, S1.Pin_2, S2.Pin_1, S2.Pin_2, LED1.cathode, LED2.cathode, S3.Pin_1, S3.Pin_2, LED3.cathode, S4.Pin_1, S4.Pin_2, LED4.cathode, S5.Pin_1, S5.Pin_2, LED5.cathode, Part2.GND, Part3.GND, SG1.2
  N4: Part1.D8_PWM, SG1.1
  3V3: Part1.3V3, Part2.3.3V
  5V: Part1.5V, U1.E, Part3.VCC
  N5: Part1.D22, LED1.anode
  N6: Part1.D23, S1.Pin_3, S1.Pin_4
  N7: Part1.D24, LED2.anode
  N8: Part1.D25, S2.Pin_3, S2.Pin_4
  N9: Part1.D26, LED3.anode
  N10: Part1.D27, S3.Pin_3, S3.Pin_4
  N11: Part1.D28, LED4.anode
  N12: Part1.D29, S4.Pin_3, S4.Pin_4
  N13: Part1.D30, LED5.anode
  N14: Part1.D31, S5.Pin_3, S5.Pin_4
  N15: Part1.D49, Part2.RST
  N16: Part1.D50, Part2.MISO
  N17: Part1.D51, Part2.MOSI
  N18: Part1.D52, Part2.SCK
  N19: Part1.D53, Part2.SDA

custom parts:
  RFID-RC522-v2: A simple China made RFID-RC522 Reader; do check the pin labels, as this is a MFRC522 based clone.
  LCD1602-I2C: A standard character display, usually with 2x16 characters. Comes in many colors with LCM1602 IIC attached.
  Buzzer 12mm: Buzzer 12mm Spark Fun Electronics SKU : Comp-Buzzer Through hole This is a small 12mm round speaker that operates around the audible 2kHz range. You can use these speakers to create simple music or user interfaces. This is not a true piezoelectric speaker but behaves similarly. Instead of a piezoelectric crystal that vibrates with an electric current, this tiny speaker uses an electromagnet to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
